# Fritzing sketch wiring (saved by Fritzing 1.0.4)
breadboards: 1

parts:
  MCU = Esp32-c3 super mini
  DHT = Humidity and Temperature Sensor DHT11
  OLED = OLED 0.96" 128x64 I2C SSD1306
  R1 = Resistor [tolerance=±5% power=0.25W resistance=10k package=THT]
  S1 = Pushbutton [package="[THT]"]

nets:
  N1: MCU.Pin_1, OLED.SCL
  N2: MCU.Pin_5, S1.Pin_1, S1.Pin_2
  N3: MCU.Pin_6, DHT.Data, R1.Pin_1
  N4: MCU.Pin_13, OLED.SCA
  VCC: MCU.Pin_14, DHT.Vcc, OLED.VCC, R1.Pin_0
  GND: MCU.Pin_15, DHT.GND, OLED.GND, S1.Pin_3, S1.Pin_4
  5V: MCU.Pin_16

custom parts:
  Esp32-c3 super mini: ESP32-C3 Development Board ESP32 SuperMini Development Board ESP32 Development Board WiFi Bluetooth.
  Humidity and Temperature Sensor DHT11: Digital relative humidity & temperature sensor DHT11
